# Fritzing sketch circuit diagram (saved by Fritzing 0.9.3b)
breadboards: 3

parts:
  Bauteil1 = Arduino Uno (Rev3)
  BLUE = LEDs [package=led10mm]
  R3 = Resistor [tolerance=±5% resistance=560 package="1206 [SMD]"]
  R2 = Resistor [tolerance=±5% resistance=560 package="1206 [SMD]"]
  GREEN = LEDs [package=led10mm]
  RED = LEDs [package=led10mm]
  R1 = Resistor [tolerance=±5% resistance=560 package="1206 [SMD]"]
  Bauteil2 = Adafruit ADXL377 [part_number="Adafruit #1413"]
  R4 = Resistor [tolerance=±5% resistance=220 package=THT]
  S1 = Pushbutton [package="[THT]"]
  S2 = Pushbutton [package="[THT]"]
  R5 = Resistor [tolerance=±5% resistance=10k package=THT]
  C1 = Electrolytic Capacitor [capacitance=100nF package="1010 [SMD, electrolytic]"]
  Bauteil3 = Arduino MicroSD Shield  # not connected

nets:
  N1: Bauteil1.A0, Bauteil2.XOUT
  N2: Bauteil1.A1, Bauteil2.YOUT
  N3: Bauteil1.A2, Bauteil2.ZOUT
  N4: Bauteil1.D8, R3.Pin_0
  N5: Bauteil1.D9_PWM, R2.Pin_0
  N6: Bauteil1.D10_PWM/SS, R1.Pin_0
  GND: Bauteil1.GND, BLUE.C, GREEN.C, RED.C, Bauteil2.GND, S1.Pin_1, S1.Pin_2, R5.Pin_1, C1.+
  N7: Bauteil1.AREF, Bauteil2.3.3V
  N8: Bauteil1.D2, R4.Pin_1, S1.Pin_3, S1.Pin_4
  5V: Bauteil1.D4, Bauteil1.5V, Bauteil2.VIN, R4.Pin_0, S2.Pin_3, S2.Pin_4
  N9: BLUE.A, R3.Pin_1
  N10: R2.Pin_1, GREEN.A
  N11: RED.A, R1.Pin_1
  N12: S2.Pin_1, S2.Pin_2, R5.Pin_0, C1.-

custom parts:
  Adafruit ADXL377: Hey rocket man (burnin' out your fuse out there alone) ever wonder how fast you're rocketing? The ADXL377 +-200g 3-axis accelerometer may be able to tell the answer. You read that right, this accelerometer can sense up to 200g's of force. Incredible! Not surprisingly, we couldn't say "no" to a breakout for this sensor. The sensor is soldered onto a PCB with four mounting holes (in case you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
