# Fritzing sketch code_and_diagramm (saved by Fritzing 0.9.3b)
breadboards: 1

parts:
  Bauteil1 = Arduino Uno (Rev3) - ICSP  # not connected
  Bauteil2 = Arduino MicroSD Shield
  Bauteil3 = Adafruit ADXL377 [part_number="Adafruit #1413"]
  LED1 = LEDs [package=led10mm]
  LED2 = LEDs [package=led10mm]
  R1 = Resistor [tolerance=±5% resistance=220 package=THT]
  R2 = Resistor [tolerance=±5% resistance=220 package=THT]
  S1 = Pushbutton [package="[SMD]"]
  R3 = Resistor [tolerance=±5% resistance=10k package=THT]

nets:
  5V: Bauteil2.5V, Bauteil3.VIN, S1.Pin_1, S1.Pin_2
  N1: Bauteil2.A1, Bauteil3.ZOUT
  N2: Bauteil2.A2, Bauteil3.YOUT
  N3: Bauteil2.A3, Bauteil3.XOUT
  N4: Bauteil2.AREF, Bauteil3.3.3V
  N5: Bauteil2.D2, S1.Pin_3, S1.Pin_4, R3.Pin_1
  N6: Bauteil2.D6, R1.Pin_1
  N7: Bauteil2.D7, R2.Pin_1
  GND: Bauteil2.GND, Bauteil3.GND, LED1.C, LED2.C, R3.Pin_0
  N8: LED1.A, R1.Pin_0
  N9: LED2.A, R2.Pin_0

custom parts:
  Adafruit ADXL377: Hey rocket man (burnin' out your fuse out there alone) ever wonder how fast you're rocketing? The ADXL377 +-200g 3-axis accelerometer may be able to tell the answer. You read that right, this accelerometer can sense up to 200g's of force. Incredible! Not surprisingly, we couldn't say "no" to a breakout for this sensor. The sensor is soldered onto a PCB with four mounting holes (in case you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

// code stored in the sketch: bmts.ino
/*
   Author: Fabian Schwab
   Version: 1.0
   Required:
      Hardware:
        - Adruino Uno
        - Sparkfun SD shield
        - Adafruit ADXL377 sensor
      Software:
        - SD Library
        - SPI Library
        - ADXL377 Library
   Description:
        - This devices measures the maximum G and saves it to a *.csv file

*/

#include <SD.h>
#include <SPI.h>
#include <ADXL377.h>

/*
   Senor unsing analog pin A3 for X-axis, A2 for Y-axis and A1 for Z-axis
   You may have to change this pins if you have choosen a different setup on your board
*/
ADXL377 acc(A3, A2, A1);

// The Sparkfun microSD shield uses pin 8 for CS
const int chipSelect = 8;

/*
   This prefixes are used for the folder and file structure.
   Each time the arduion is turned on the folders get a higher number,
   so that each testing sequence is in its own foder.

   For the *.csv files it's the same,
   except that afer each recording the number at the end is increased.
*/
const String folderPrefix = "squ_";
const String filePrefix = "tst_";

//Contains the whole folder name as seen on the SD card.
//It's just there to buffer the name for all iteratinos of the main loop
String folderName;

File file;
int fileCount = 0;

//Determine the time for the recording of the forces
const int recTimeInSeconds = 10;

/*
   Recording Mode
      1. Record all data for the entire time.
      2. Record only the maximum over time.
*/
const int mode = 1;

void setup()
{


  Serial.begin(9600);
  while (!Serial) {

  }

  //Serial.print("Initializing SD card... ");
  /*
      Note that even if it's not used as the CS pin, the hardware SS pin
      (10 on most Arduino boards, 53 on the Mega) must be left as an output
      or the SD library functions will not work.
  */
  pinMode(10, OUTPUT);

  if (!SD.begin(chipSelect)) {
    //Serial.println("initialization failed!");
    exit(1);
  }
  //Serial.println("initialization done.");
  folderSetup();
}

void folderSetup() {
  int counter = 0;

  //Serial.println("Fetching folder... ");

  do {
    folderName = folderPrefix + String(counter);
    counter++;
  } while (SD.exists(folderName));

  if (SD.mkdir(folderName)) {
    Serial.println(folderName + " created.");
    return folderName;
  }
  Serial.println("failed creating folder: " + folderName);
  exit(1);
}

void loop()
{
  String fileName = filePrefix + String(fileCount) + ".csv";
  fileCount++;

  file = SD.open(folderName + "/" + fileName, FILE_WRITE);

  // if the file opened okay, write to it:
  if (file) {
    Serial.println("Ready to log data...");
    digitalWrite(6, HIGH);
    digitalWrite(7, LOW);
    bool isReady = true;
    while (isReady) {
      if (digitalRead(2) == HIGH) {
        isReady = false;
        digitalWrite(7, HIGH);
        digitalWrite(6, LOW);
      }
    }
    file.println("Time;X;Y;Z;");
    unsigned int limit = millis() + recTimeInSeconds * 1000;
    if (mode == 1) {
      while (millis() <= limit) {
        file.print(millis());
        file.print(";");
        file.print(acc.getX());
        file.print(";");
        file.print(acc.getY());
        file.print(";");
        file.print(acc.getZ());
        file.println(";");
      }
      if (mode == 2) {

      }
    }
    digitalWrite(7, LOW);
    file.close();
  } else {
    Serial.print("Cannot open file to log data...");
  }
}
